# Fritzing sketch alarm_schema (saved by Fritzing 0.9.3b)
breadboards: 1

parts:
  Součástka2 = Logic Level Converter
  LED1 = LED - 5mm [color="Red (633nm)" package="5 mm [THT]"]
  LED2 = LED - 5mm [color="Green (570nm)" package="5 mm [THT]"]
  Matrix_keypad1 = KEYPAD 4x4
  Součástka3 = Breadboard Power Supply Board SMD
  Espessif_Serial_Wifi_Modul_1 = ESP8266 ESP01 [part_number=ESP8266 package=THT]
  R3 = Resistor [tolerance=±5% resistance=4.7k package=THT]
  PIR1 = PIR sensor
  Součástka4 = Arduino Nano (Rev3.0)
  R1 = Resistor [tolerance=±5% resistance=10k package="0805 [SMD]"]
  C2 = Electrolytic Capacitor [capacitance=1µF voltage=16V package="1010 [SMD, electrolytic]"]

nets:
  N1: Součástka2.TX2_LV, Espessif_Serial_Wifi_Modul_1.RXD
  N2: Součástka2.RX2_LV, Espessif_Serial_Wifi_Modul_1.TXD
  GND: Součástka2.GND, Součástka3.GND, Espessif_Serial_Wifi_Modul_1.GND, PIR1.GND, Součástka4.GND, R1.Pin_1, C2.-
  VCC: Součástka2.LV, Součástka3.VCC, Espessif_Serial_Wifi_Modul_1.VCC, C2.+
  N3: Součástka2.RX2_HV, Součástka4.D10
  N4: Součástka2.TX2_HV, Součástka4.D12/MISO
  N5: LED1.cathode, Součástka4.A4
  N6: LED1.anode, LED2.anode, R1.Pin_0
  N7: LED2.cathode, Součástka4.A5
  N8: Matrix_keypad1.col1, Součástka4.D9
  N9: Matrix_keypad1.col2, Součástka4.D8
  N10: Matrix_keypad1.col3, Součástka4.D7
  N11: Matrix_keypad1.col4, Součástka4.D6
  N12: Matrix_keypad1.row1, Součástka4.D5
  N13: Matrix_keypad1.row2, Součástka4.D4
  N14: Matrix_keypad1.row3, Součástka4.D3
  N15: Matrix_keypad1.row4, Součástka4.D2
  N16: Espessif_Serial_Wifi_Modul_1.CH_PD, R3.Pin_1
  VDD: PIR1.VDD, Součástka4.VIN
  N17: PIR1.SIG, Součástka4.D11/MOSI

custom parts:
  KEYPAD 4x4: Matrix keypad 16 buttons, 4 rows x 4 columns
  ESP8266 ESP01: Generic WiFi Module based on the ESP8266 with onboard PCB antenna and UART communications
